// Digital circuit 1-bit-register-design.dig as structural Verilog
module _1_bit_register_design (
  input  LOAD,
  input  DATA,
  input  CLOCK,
  output OUT
);

  wire and_1_out, and_2_out, not_1_out, or_1_out;

  not not_1 (not_1_out, LOAD);
  and and_1 (and_1_out, OUT, not_1_out);
  and and_2 (and_2_out, LOAD, DATA);
  or or_1 (or_1_out, and_1_out, and_2_out);
  D_FF d_ff_1 (.D(or_1_out), .C(CLOCK), .Q(OUT));  // open: nQ
endmodule
