// Digital circuit 8-bit register-design.dig as structural Verilog
module _8_bit_register_design (
  input  LOAD,
  input  D0,
  input  D1,
  input  D2,
  input  D3,
  input  D4,
  input  D5,
  input  D6,
  input  D7,
  input  in_10,
  input  in_11,
  input  in_12,
  input  clk,
  output OUT0,
  output OUT1,
  output OUT2,
  output OUT3,
  output OUT4,
  output OUT5,
  output OUT6,
  output OUT7,
  output CLOCK
);

  wire and_1_out, and_2_out, and_3_out, and_4_out, and_5_out, and_6_out, and_7_out, and_8_out, and_9_out,
       and_10_out, and_11_out, and_12_out, and_13_out, and_14_out, and_15_out, and_16_out, and_17_out,
       and_18_out, not_1_out, not_2_out, not_3_out, not_4_out, not_5_out, not_6_out, not_7_out, not_8_out,
       not_9_out, not_10_out, or_1_out, or_2_out, or_3_out, or_4_out, or_5_out, or_6_out, or_7_out, or_8_out,
       or_9_out;

  not not_1 (not_1_out, LOAD);
  not not_2 (not_2_out, LOAD);
  not not_3 (not_3_out, LOAD);
  not not_4 (not_4_out, LOAD);
  not not_5 (not_5_out, LOAD);
  not not_6 (not_6_out, LOAD);
  not not_7 (not_7_out, LOAD);
  not not_8 (not_8_out, LOAD);
  and and_1 (and_1_out, OUT0, not_1_out);
  and and_2 (and_2_out, LOAD, D0);
  and and_3 (and_3_out, OUT1, not_2_out);
  and and_4 (and_4_out, LOAD, D1);
  and and_5 (and_5_out, OUT2, not_3_out);
  and and_6 (and_6_out, LOAD, D2);
  and and_7 (and_7_out, OUT3, not_4_out);
  and and_8 (and_8_out, LOAD, D3);
  and and_9 (and_9_out, OUT4, not_5_out);
  and and_10 (and_10_out, LOAD, D4);
  and and_11 (and_11_out, OUT5, not_6_out);
  and and_12 (and_12_out, LOAD, D5);
  and and_13 (and_13_out, OUT6, not_7_out);
  and and_14 (and_14_out, LOAD, D6);
  and and_15 (and_15_out, OUT7, not_8_out);
  and and_16 (and_16_out, LOAD, D7);
  or or_1 (or_1_out, and_1_out, and_2_out);
  or or_2 (or_2_out, and_3_out, and_4_out);
  or or_3 (or_3_out, and_5_out, and_6_out);
  or or_4 (or_4_out, and_7_out, and_8_out);
  or or_5 (or_5_out, and_9_out, and_10_out);
  or or_6 (or_6_out, and_11_out, and_12_out);
  or or_7 (or_7_out, and_13_out, and_14_out);
  or or_8 (or_8_out, and_15_out, and_16_out);
  D_FF d_ff_1 (.D(or_1_out), .C(CLOCK), .Q(OUT0));  // open: nQ
  D_FF d_ff_2 (.D(or_2_out), .C(CLOCK), .Q(OUT1));  // open: nQ
  D_FF d_ff_3 (.D(or_3_out), .C(CLOCK), .Q(OUT2));  // open: nQ
  D_FF d_ff_4 (.D(or_4_out), .C(CLOCK), .Q(OUT3));  // open: nQ
  D_FF d_ff_5 (.D(or_5_out), .C(CLOCK), .Q(OUT4));  // open: nQ
  D_FF d_ff_6 (.D(or_6_out), .C(CLOCK), .Q(OUT5));  // open: nQ
  D_FF d_ff_7 (.D(or_7_out), .C(CLOCK), .Q(OUT6));  // open: nQ
  D_FF d_ff_8 (.D(or_8_out), .C(CLOCK), .Q(OUT7));  // open: nQ
  not not_9 (not_9_out, in_10);
  not not_10 (not_10_out, in_12);
  and and_17 (and_17_out, clk, in_10);
  and and_18 (and_18_out, not_9_out, in_11);
  or or_9 (or_9_out, and_17_out, and_18_out);
  and and_19 (CLOCK, or_9_out, not_10_out);

  // Notes on the sheet:
  //   8-BIT-INPUT
  //   8-BIT-OUTPUT
  //   Clock Logic
  //   Astable Pulse
  //   Manual Pulse
  //   Select
  //   HLT
endmodule
