// Digital circuit 8-bit-register-uisng-digital-ic.dig as structural Verilog
module _8_bit_register_uisng_digital_ic (
  input  RESET,
  input  LOAD,
  input  D0,
  input  D1,
  input  D2,
  input  D3,
  input  D4,
  input  D5,
  input  D6,
  input  D7,
  input  DISABLE,
  input  CLOCK,
  output OUT7,
  output OUT6,
  output OUT5,
  output OUT4,
  output out_5,
  output OUT3,
  output OUT1,
  output OUT0,
  output OUT2
);

  wire _74173_1_pin3, _74173_1_pin4, _74173_1_pin5, _74173_1_pin6, _74173_2_pin3, _74173_2_pin4,
       _74173_2_pin5, _74173_2_pin6, not_1_out;

  not not_1 (not_1_out, LOAD);
  _74173 _74173_1 (
    .pin1(1'b0), .pin2(1'b0), .pin3(_74173_1_pin3), .pin4(_74173_1_pin4), .pin5(_74173_1_pin5),
    .pin6(_74173_1_pin6), .pin7(CLOCK), .pin8(1'b0), .pin9(not_1_out), .pin10(not_1_out), .pin11(D3),
    .pin12(D2), .pin13(D1), .pin14(D0), .pin15(RESET), .pin16(1'b1));
  _74173 _74173_2 (
    .pin1(1'b0), .pin2(1'b0), .pin3(_74173_2_pin3), .pin4(_74173_2_pin4), .pin5(_74173_2_pin5),
    .pin6(_74173_2_pin6), .pin7(CLOCK), .pin8(1'b0), .pin9(not_1_out), .pin10(not_1_out), .pin11(D7),
    .pin12(D6), .pin13(D5), .pin14(D4), .pin15(RESET), .pin16(1'b1));
  _74245 _74245_1 (
    .pin1(1'b1), .pin2(_74173_1_pin3), .pin3(_74173_1_pin4), .pin4(_74173_1_pin5), .pin5(_74173_1_pin6),
    .pin6(_74173_2_pin3), .pin7(_74173_2_pin4), .pin8(_74173_2_pin5), .pin9(_74173_2_pin6), .pin10(1'b0),
    .pin11(OUT7), .pin12(OUT6), .pin13(OUT5), .pin14(OUT4), .pin15(OUT3), .pin16(OUT2), .pin17(OUT1),
    .pin18(OUT0), .pin19(DISABLE), .pin20(1'b1));

  assign out_5 = OUT4;

  // Notes on the sheet:
  //   4-BIT D-Type Register
  //   Octal Bus Transceivers
  //   BUS
endmodule
