// Digital circuit Clock-Logic.dig as structural Verilog
module Clock_Logic (
  input  in_2,
  input  in_3,
  input  in_4,
  input  clk,
  output out_1
);

  wire and_1_out, and_2_out, not_1_out, not_2_out, or_1_out;

  not not_1 (not_1_out, in_2);
  not not_2 (not_2_out, in_4);
  and and_1 (and_1_out, clk, in_2);
  and and_2 (and_2_out, not_1_out, in_3);
  or or_1 (or_1_out, and_1_out, and_2_out);
  and and_3 (out_1, or_1_out, not_2_out);

  // Notes on the sheet:
  //   Clock Logic
  //   Astable Pulse
  //   Manual Pulse
  //   Select
  //   HLT
endmodule
