// Digital circuit Latch-vs-Flip-Flop.dig as structural Verilog
module Latch_vs_Flip_Flop (
  input  EN,
  input  D,
  input  Clock,
  output Q_latch,
  output Q,
  output Q_flipflop
);

  wire and_1_out, and_2_out, not_1_out;

  not not_1 (not_1_out, D);
  and and_1 (and_1_out, not_1_out, EN);
  and and_2 (and_2_out, EN, D);
  D_FF d_ff_1 (.D(D), .C(Clock), .Q(Q_flipflop));  // open: nQ
  nor nor_1 (Q_latch, and_1_out, Q);
  nor nor_2 (Q, Q_latch, and_2_out);

  // Notes on the sheet:
  //   D Latch
  //   D FlipFlop
endmodule
