// Digital circuit S-R-Latch-with-Enable.dig as structural Verilog
module S_R_Latch_with_Enable (
  input  EN,
  input  R,
  input  S,
  output Q,
  output Q_2
);

  wire and_1_out, and_2_out;

  and and_1 (and_1_out, R, EN);
  and and_2 (and_2_out, EN, S);
  nor nor_1 (Q, and_1_out, Q_2);
  nor nor_2 (Q_2, Q, and_2_out);

  // Notes on the sheet:
  //   S-R latch with enable
endmodule
