// Digital circuit S-R-Latch.dig as structural Verilog
module S_R_Latch (
  input  R,
  input  S,
  output Q,
  output Q_2
);

  nor nor_1 (Q, R, Q_2);
  nor nor_2 (Q_2, Q, S);

  // Notes on the sheet:
  //   S-R latch
endmodule
